# Fritzing sketch pico_sh1106 (saved by Fritzing 0.9.3b)
breadboards: 1

parts:
  SH1106_128_x_64 = OLED 128x64 I2C Monochrome Display
  S2 = Pushbutton [package=THT]
  Mod2 = Raspberry Pi Pico W

nets:
  N1: SH1106_128_x_64.SDA, Mod2.pin_6
  N2: SH1106_128_x_64.SCK, Mod2.pin_7
  N3: SH1106_128_x_64.VDD, Mod2.pin_36
  N4: SH1106_128_x_64.GND, S2.leg0, Mod2.pin_3, Mod2.pin_8, Mod2.pin_13, Mod2.pin_18, Mod2.pin_23, Mod2.pin_28, Mod2.pin_33, Mod2.pin_38
  N5: S2.leg1, Mod2.pin_30

custom parts:
  Raspberry Pi Pico W: Raspberry Pi Pico W. Based around the RP2040 microcontroller the Pico W is a low cost microcontroller device bringing Raspberry Pi quality, cost, and easy of use to the microcontroller space. The areas marked KEEPOUT in pcb silkscreen should not have traces running through them to avoid shorts on a soldered in module!
